# Fritzing sketch Color Sensor (saved by Fritzing 0.9.2b)
breadboards: 1

parts:
  Part1 = Adafruit TCS34725 RGB Color Sensor [part_number="Adafruit #1334"]
  Part2 = Arduino Uno (Rev3)

nets:
  VIN: Part1.VIN, Part2.5V
  GND: Part1.GND, Part2.GND
  N1: Part1.SCL, Part2.A5/SCL
  N2: Part1.SDA, Part2.A4/SDA

custom parts:
  Adafruit TCS34725 RGB Color Sensor: Your electronics can now see in dazzling color with this lovely color light sensor. We found the best color sensor on the market, the TCS34725, which has RGB and Clear light sensing elements. An IR blocking filter, integrated on-chip and localized to the color sensing photodiodes, minimizes the IR spectral component of the incoming light and allows color measurements to be made accurately. The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
