# Fritzing sketch Color-Sensor-RGB (saved by Fritzing 0.9.2b)
breadboards: 1

parts:
  Part1 = Adafruit TCS34725 RGB Color Sensor [part_number="Adafruit #1334"]
  Part2 = Arduino Uno (Rev3)
  LED1 = RGB LED (com. cathode, rbg) [package="5 mm [THT]"]
  R1 = Resistor [tolerance=±5% resistance=220 package="0402 [SMD]"]
  R2 = Resistor [tolerance=±5% resistance=220 package="0402 [SMD]"]
  R3 = Resistor [tolerance=±5% resistance=220 package="0402 [SMD]"]

nets:
  N1: Part1.SCL, Part2.A5/SCL
  N2: Part1.SDA, Part2.A4/SDA
  N3: Part2.D3_PWM, R3.Pin_1
  N4: Part2.D5_PWM, R2.Pin_1
  N5: Part2.D6_PWM, R1.Pin_1
  N6: Part2.GND, LED1.common_cathode
  N7: LED1.red_anode, R3.Pin_0
  N8: LED1.blue_anode, R2.Pin_0
  N9: LED1.green_anode, R1.Pin_0

custom parts:
  Adafruit TCS34725 RGB Color Sensor: Your electronics can now see in dazzling color with this lovely color light sensor. We found the best color sensor on the market, the TCS34725, which has RGB and Clear light sensing elements. An IR blocking filter, integrated on-chip and localized to the color sensing photodiodes, minimizes the IR spectral component of the incoming light and allows color measurements to be made accurately. The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
