# Fritzing sketch DHT22Pinout (saved by Fritzing 0.9.2b)
breadboards: 1

parts:
  DHT1 = DHT22 Humidity and Temperature Sensor
  Part1 = Arduino Uno (Rev3)
  R1 = Resistor [tolerance=±5% resistance=10k package=THT]

nets:
  VDD: DHT1.VDD, Part1.5V, R1.Pin_1
  N1: DHT1.DATA, Part1.D10_PWM/SS, R1.Pin_0
  GND: DHT1.GND, Part1.GND
